# Fritzing sketch connections (saved by Fritzing 0.9.3b)

parts:
  WeMos_D1_Mini1 = WeMos D1 Mini
  J1 = Basic Servo
  J2 = Basic Servo
  S1 = Pushbutton [package=THT]
  S2 = Pushbutton [package=THT]
  S3 = Pushbutton [package=THT]
  S4 = Pushbutton [package=THT]
  LED1 = LED - 3mm [color="Red (633nm)" package="3 mm [THT]"]
  R1 = Resistor [tolerance=±5% resistance=1k package=THT]
  Part1 = Lilypad Battery Connect

nets:
  VCC: WeMos_D1_Mini1.5V, J1.vcc, J2.vcc, Part1.+
  N1: WeMos_D1_Mini1.D0, R1.Pin_1
  N2: WeMos_D1_Mini1.D1, S2.leg0
  N3: WeMos_D1_Mini1.D2, S1.leg0
  N4: WeMos_D1_Mini1.D3, J1.pulse
  N5: WeMos_D1_Mini1.D4, J2.pulse
  N6: WeMos_D1_Mini1.D5, S3.leg0
  N7: WeMos_D1_Mini1.D6, S4.leg0
  GND: WeMos_D1_Mini1.G, J1.gnd, J2.gnd, S1.leg1, S2.leg1, S3.leg1, S4.leg1, LED1.anode, Part1.-
